# Fritzing sketch Arduino101_LED (saved by Fritzing 0.9.3b)
breadboards: 1

parts:
  元件1 = Genuino 101
  LED1 = smd LED [color="Red (633nm)" package="0805 [SMD]"]
  R1 = Resistor [tolerance=±5% resistance=220 package=THT]

nets:
  N1: 元件1.D9_PWM, LED1.anode
  N2: 元件1.GND, R1.Pin_0
  N3: LED1.cathode, R1.Pin_1

custom parts:
  Genuino 101: A learning and development board that delivers the performance and low-power consumption of the Intel® Curie™ Module with the simplicity of Arduino at an entry-level price. It keeps the same robust form factor and peripheral list of the UNO with the addition of onboard Bluetooth LE capabilities and a 6-axis accelerometer/gyro to help you easily expand your creativity into the connected world.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
